# Fritzing sketch Acquar-ino (saved by Fritzing 0.8.7b)
breadboards: 1

parts:
  ESP8267 = NodeMCU V1.0
  LUCE = KY-019 5V Relay Module [package="Breakout board"]
  Componente1 = Arduino Uno (Rev3)
  RTC_DS1302 = RTC_DS1302_module
  PH_SENSOR = PH meter [package=THT]
  DS2 = DS18B20 1-Wire Temperature Sensor [part_number=DS18B20]
  R1 = Resistor [tolerance=±5% resistance=220 package=THT]
  AREATORE = KY-019 5V Relay Module [package="Breakout board"]
  POMPA = KY-019 5V Relay Module [package="Breakout board"]
  MANGIATOIA = Basic Servo
  GALLEGGIANTE = Square Pushbutton
  R2 = Resistor [tolerance=±5% resistance=10k package=THT]
  U1 = LM2596 step down module
  230_V = Power plug
  12_v = Power plug

nets:
  N1: ESP8267.D2, Componente1.D1/TX
  N2: ESP8267.D3, Componente1.D0/RX
  N3: ESP8267.D4, RTC_DS1302.DAT
  3V3: ESP8267.3V3, Componente1.3V3, RTC_DS1302.VCC
  GND: ESP8267.GND, LUCE.-, Componente1.GND, RTC_DS1302.GND, PH_SENSOR.pin3, DS2.GND, AREATORE.-, POMPA.-, MANGIATOIA.gnd, R2.Pin_0, U1.IN-, U1.OUT-, 12_v.GND
  N4: ESP8267.D5, RTC_DS1302.CLK
  N5: ESP8267.D6, RTC_DS1302.RST
  N6: LUCE.S, Componente1.D5_PWM
  5V: LUCE.+, Componente1.5V, PH_SENSOR.pin2, DS2.VDD, R1.Pin_1, AREATORE.+, POMPA.+, MANGIATOIA.vcc, GALLEGGIANTE.leg1, U1.OUT+
  N7: LUCE.Common, AREATORE.Common, POMPA.Common, 230_V.GND
  N8: LUCE.NO, AREATORE.NO, POMPA.NO, 230_V.VCC
  N9: Componente1.A1, PH_SENSOR.pin1
  N10: Componente1.D8, GALLEGGIANTE.leg0, R2.Pin_1
  N11: Componente1.D9_PWM, MANGIATOIA.pulse
  N12: Componente1.D2, DS2.DQ, R1.Pin_0
  N13: Componente1.D6_PWM, AREATORE.S
  N14: Componente1.D7, POMPA.S
  N15: U1.IN+, 12_v.VCC

notes:
  Sensore Temperatura

custom parts:
  NodeMCU V1.0: ESP8266 based NodeMCU
  KY-019 5V Relay Module: KY-019 5V Relay module, used to control AC circuits.
  RTC_DS1302_module: Arduino module DS1302 SPI Real Time Clock
  LM2596 step down module: LM2596 DC-DC step down power supply module 3 A.
